# Fritzing sketch Doorbot 1.41421356237 (saved by Fritzing 0.9.3b)
circuit board: 5.36311cm x 6.88566cm
breadboards: 1

parts:
  Raspberry_Pi_1 = Raspberry Pi 3 [part_number=RPI-3-V1.2]
  Part1 = Arduino Uno (Rev3)
  Power_In = screw terminal, 3 pins
  U1 = Voltage Regulator - 5V [package="DPak [SMD]"]
  D2 = Rectifier Diode [part_number=1N4004 package="Melf DO-213 AB [SMD]"]
  C1 = Electrolytic Capacitor [capacitance=47µF voltage=35V package="0405 [SMD, electrolytic]"]
  D1 = Rectifier Diode [part_number=1N4004 package="Melf DO-213 AB [SMD]"]
  C2 = Ceramic Capacitor [capacitance=1µF voltage=16V package="1206 [SMD, multilayer]"]
  Relay_Board = female pin header, 8 pins [form="♀ (female)"]
  RFID = double row female pin header, 10 pins [form="♀ (female)"]
  U2 = Voltage Regulator - 5V [package="TO220 [THT]"]
  Door_Sense = screw terminal, 3 pins
  C3 = Electrolytic Capacitor [capacitance=10µF voltage=16V package="0405 [SMD, electrolytic]"]
  R1 = Resistor [tolerance=±5% resistance=10k package="0805 [SMD]"]
  C4 = Ceramic Capacitor [capacitance=1µF voltage=16V package="1206 [SMD, multilayer]"]
  C5 = Ceramic Capacitor [capacitance=100nF voltage=16V package="1206 [SMD, multilayer]"]
  C6 = Ceramic Capacitor [capacitance=1µF voltage=16V package="1206 [SMD, multilayer]"]

nets:
  GND: Raspberry_Pi_1.GND, Part1.GND, Power_In.pin2, U1.GND, C1.-, C2.0, Relay_Board.pin1, Relay_Board.pin2, Relay_Board.pin7, RFID.pin5, RFID.pin10, U2.GND, C3.-, C4.1, C5.1, C6.0
  5V: Raspberry_Pi_1.5V, Part1.5V, U1.output_voltage, C2.1, Relay_Board.pin8, RFID.pin1, RFID.pin6, U2.output_voltage, C3.+, R1.Pin_1, C4.0, C5.0, C6.1
  N1: Part1.D8, Relay_Board.pin6
  N2: Part1.D9_PWM, Relay_Board.pin5
  N3: Part1.D10_PWM/SS, Relay_Board.pin4
  N4: Part1.D11_PWM/MOSI, Relay_Board.pin3
  N5: Part1.D2, RFID.pin3, RFID.pin8
  N6: Part1.D3_PWM, RFID.pin2, RFID.pin4, RFID.pin7, RFID.pin9
  N7: Part1.D4, Door_Sense.pin1
  N8: Part1.D5_PWM, Door_Sense.pin2
  N9: Power_In.pin1, D1.anode
  N10: Power_In.pin3, D2.anode
  N11: U1.input_voltage, D2.cathode, C1.+, D1.cathode, U2.input_voltage
  N12: Door_Sense.pin3, R1.Pin_0

notes:
  Doorbot 1.41421356237
